# Fritzing sketch circuit (saved by Fritzing 0.9.3b)
breadboards: 1
perfboards: 1

parts:
  7_4V2 = Header 2 [package=molex-1x2_lock]
  Float_Switch1 = Header 2 [package=molex-1x2_lock]
  D4 = Rectifier Diode [part_number=1N4001 package="300 mil [THT]"]
  R16 = Resistor [tolerance=±5% resistance=10k package="1206 [SMD]"]
  R17 = Resistor [tolerance=±5% resistance=10k package="1206 [SMD]"]
  R19 = Resistor [tolerance=±5% resistance=1k package="1206 [SMD]"]
  R20 = Resistor [tolerance=±5% resistance=1k package="1206 [SMD]"]
  3_7V1 = Header 2 [package=molex-1x2_lock]
  IC1 = Voltage Regulator [package=to-92]
  ESP-12S = Gizwits WiFi Witty ESP-12F
  R18 = Resistor [tolerance=±5% resistance=10k package="1206 [SMD]"]
  Q2_IRL540N = Basic FET N-Channel [package="TO220 [THT]"]
  soil_moisture_sensor = FC-28 Soil Hygrometer Module
  Soil_Moisture_Sensor = Header 2 [package=molex-1x2_lock]
  C2_10uf = Capacitor Polarized [package=cpol-radial-10uf-25v]
  C1_10uf = Capacitor Polarized [package=cpol-radial-10uf-25v]
  Q2_IRL540N1 = Basic FET N-Channel [package="TO220 [THT]"]
  Mortor1 = Header 2 [package=molex-1x2_lock]

nets:
  N1: 7_4V2.1, D4.cathode, Mortor1.1
  GND: 7_4V2.2, Float_Switch1.2, R17.Pin_1, 3_7V1.2, IC1.GND, ESP-12S.GND, R18.Pin_1, Q2_IRL540N.source, C2_10uf.-, C1_10uf.-, Q2_IRL540N1.source
  N2: Float_Switch1.1, R16.Pin_0, ESP-12S.GPIO5
  N3: D4.anode, Q2_IRL540N1.drain, Mortor1.2
  3.3V: R16.Pin_1, IC1.OUT, ESP-12S.VCC, soil_moisture_sensor.VCC, C2_10uf.+
  N4: R17.Pin_0, R19.Pin_0, ESP-12S.GPIO14
  N5: R19.Pin_1, Q2_IRL540N1.gate
  N6: R20.Pin_0, ESP-12S.GPIO13, R18.Pin_0
  N7: R20.Pin_1, Q2_IRL540N.gate
  N8: 3_7V1.1, IC1.IN, C1_10uf.+
  N9: ESP-12S.REST, ESP-12S.GPIO16
  N10: ESP-12S.GPIO4, soil_moisture_sensor.DO
  N11: Q2_IRL540N.drain, soil_moisture_sensor.GND
  N12: soil_moisture_sensor.POS, Soil_Moisture_Sensor.2
  N13: soil_moisture_sensor.NEG, Soil_Moisture_Sensor.1

custom parts:
  FC-28 Soil Hygrometer Module: The FC-28 is a soil hygrometer module that uses the Texas Instruments LM393 comparator chip to provide an analog measurement of soil humidity. The digital output is high when soil moisture is over a certain threshold, as determined by adjusting the potentiometer.
